// Logisim project 16BIT.circ as structural Verilog: 1 circuit, main circuit main
module main (
  input  [1:0] ARHT,
  input  in_2,
  input  in_3,
  input  HRD_RST,
  input  OE
);

  wire and_1_out, and_2_out, clock_1_out, controlled_buffer_4_out, controlled_buffer_9_out,
       controlled_buffer_10_out, controlled_buffer_12_out, controlled_buffer_13_out,
       controlled_buffer_14_out, controlled_buffer_15_out, controlled_buffer_16_out,
       controlled_buffer_34_out, controlled_buffer_35_out, d_ff_1_q, d_ff_2_q, decoder_1_out0,
       decoder_1_out1, decoder_1_out2, decoder_1_out3, decoder_1_out4, decoder_1_out5, decoder_1_out6,
       decoder_1_out7, decoder_2_out0, decoder_2_out1, decoder_2_out2, decoder_2_out3, decoder_2_out4,
       decoder_2_out5, decoder_2_out6, decoder_2_out7, decoder_3_out0, decoder_3_out1, decoder_3_out2,
       decoder_3_out3, decoder_3_out4, decoder_3_out5, decoder_3_out6, decoder_3_out7, decoder_4_out0,
       decoder_4_out1, decoder_4_out2, decoder_4_out3, decoder_4_out4, decoder_4_out5, decoder_4_out6,
       decoder_4_out7, decoder_5_out0, decoder_5_out1, decoder_5_out2, decoder_5_out3, decoder_6_out0,
       decoder_6_out1, decoder_6_out2, decoder_6_out3, demultiplexer_1_out1, demultiplexer_2_out1,
       demultiplexer_3_out0, demultiplexer_3_out1, demultiplexer_4_out0, demultiplexer_4_out1,
       demultiplexer_5_out1, demultiplexer_6_out1, demultiplexer_7_out0, demultiplexer_7_out1,
       demultiplexer_8_out0, demultiplexer_8_out1, not_1_out, not_2_out, not_3_out, or_1_out,
       pull_resistor_18_node, pull_resistor_32_node, pull_resistor_33_node, pull_resistor_35_node,
       pull_resistor_36_node, undriven_2;
  wire [1:0] counter_4_q, rom_1_data_2;
  wire [2:0] controlled_buffer_2_out, counter_2_q;
  wire [3:0] controlled_buffer_7_out, controlled_buffer_7_out_2, controlled_buffer_7_out_3,
       controlled_buffer_7_out_4, counter_3_q;
  wire [7:0] adder_1_cout, controlled_buffer_1_out, controlled_buffer_5_out, controlled_buffer_5_out_2,
       controlled_buffer_30_out, controlled_buffer_40_out, counter_1_q, IR_MEMH_q, IR_MEML_q, register_1_q,
       register_2_q, register_3_q, register_4_q, register_5_q, register_6_q, register_7_q, register_8_q,
       register_9_q, register_10_q, register_11_q, register_12_q, register_13_q, register_14_q,
       register_15_q, register_16_q, register_17_q, register_18_q, register_19_q, register_20_q,
       register_21_q, register_22_q, register_23_q, register_24_q, register_25_q, register_26_q,
       register_27_q, register_28_q, register_29_q, register_31_q, register_32_q, register_33_q,
       register_34_q, register_35_q, register_36_q, register_37_q, register_38_q, register_39_q;
  wire [15:0] adder_1_out, divider_1_out, multiplexer_2_out, multiplier_1_out, ram_1_data, register_30_q,
       rom_2_data, subtractor_1_out, undriven;
  wire [29:0] rom_1_data;

  Clock clock_1 (.out(clock_1_out));
  and and_1 (and_1_out, register_1_q[7], register_1_q[6], register_1_q[5], register_1_q[4], register_1_q[3], register_1_q[2], register_1_q[1], register_1_q[0]);
  not not_1 (not_1_out, and_1_out);
  Counter counter_1 (.count(rom_1_data[0]), .Q(counter_1_q), .clk(clock_1_out), .clr(HRD_RST));  // open: load, D, carry
  Register register_1 (.D(counter_1_q), .en(rom_1_data[1]), .Q(register_1_q), .clk(clock_1_out), .clr(HRD_RST));
  D_Flip_Flop d_ff_1 (.clk(clock_1_out), .D(and_1_out), .Q(d_ff_1_q), .reset(not_1_out));  // open: Qn, preset, en
  assign controlled_buffer_1_out = rom_1_data[2] ? register_1_q : 8'bz;  // Controlled_Buffer controlled_buffer_1
  Counter #(.width(3), .max('h7)) counter_2 (
    .load(rom_1_data[5]), .D(register_3_q[2:0]), .count(d_ff_1_q), .Q(counter_2_q), .clk(clock_1_out),
    .clr(HRD_RST));  // open: carry
  Decoder #(.select(3)) decoder_1 (
    .out0(decoder_1_out0), .out1(decoder_1_out1), .out2(decoder_1_out2), .out3(decoder_1_out3),
    .out4(decoder_1_out4), .out5(decoder_1_out5), .out6(decoder_1_out6), .out7(decoder_1_out7),
    .sel(counter_2_q), .en(1'b1));
  Decoder #(.select(3)) decoder_2 (
    .out0(decoder_2_out0), .out1(decoder_2_out1), .out2(decoder_2_out2), .out3(decoder_2_out3),
    .out4(decoder_2_out4), .out5(decoder_2_out5), .out6(decoder_2_out6), .out7(decoder_2_out7),
    .sel(counter_2_q), .en(1'b1));
  Multiplexer #(.width(8)) multiplexer_1 (
    .in0(IR_MEMH_q), .in1(IR_MEML_q), .out(controlled_buffer_1_out), .sel(rom_1_data[7]), .en(rom_1_data[6]));
  Counter #(.width(4), .max('hf)) counter_3 (
    .count(1'b1), .Q(counter_3_q), .clk(clock_1_out), .clr(or_1_out));  // open: load, D, carry
  or or_1 (or_1_out, rom_1_data[22], and_2_out);
  ROM #(.addrWidth(9), .dataWidth(32)) rom_1 (
    .addr({register_5_q[4:0], counter_3_q}), .data({rom_1_data_2, rom_1_data}));  // open: sel
  and and_2 (and_2_out, d_ff_2_q, rom_1_data[10]);
  ROM #(.dataWidth(16)) rom_2 (.addr(controlled_buffer_1_out), .data(rom_2_data), .sel(decoder_1_out0));
  ROM #(.dataWidth(16)) rom_3 (.addr(controlled_buffer_1_out), .data(rom_2_data), .sel(decoder_1_out1));
  ROM #(.dataWidth(16)) rom_4 (.addr(controlled_buffer_1_out), .data(rom_2_data), .sel(decoder_1_out2));
  ROM #(.dataWidth(16)) rom_5 (.addr(controlled_buffer_1_out), .data(rom_2_data), .sel(decoder_1_out3));
  RAM #(.dataWidth(16)) ram_1 (
    .addr(register_1_q), .data(ram_1_data), .sel(decoder_2_out0), .clk(clock_1_out), .ld(rom_1_data[9]),
    .clr(HRD_RST));
  RAM #(.dataWidth(16)) ram_2 (
    .addr(register_1_q), .data(ram_1_data), .sel(decoder_2_out1), .clk(clock_1_out), .ld(rom_1_data[9]),
    .clr(HRD_RST));
  RAM #(.dataWidth(16)) ram_3 (
    .addr(register_1_q), .data(ram_1_data), .sel(decoder_2_out2), .clk(clock_1_out), .ld(rom_1_data[9]),
    .clr(HRD_RST));
  RAM #(.dataWidth(16)) ram_4 (
    .addr(register_1_q), .data(ram_1_data), .sel(decoder_2_out3), .clk(clock_1_out), .ld(rom_1_data[9]),
    .clr(HRD_RST));
  assign controlled_buffer_2_out = rom_1_data[18] ? register_5_q[7:5] : 3'bz;  // Controlled_Buffer controlled_buffer_2
  D_Flip_Flop d_ff_2 (.clk(clock_1_out), .D(rom_1_data[10]), .Q(d_ff_2_q), .reset(HRD_RST));  // open: Qn, preset, en
  ROM #(.dataWidth(16)) rom_6 (.addr(controlled_buffer_1_out), .data(rom_2_data), .sel(decoder_1_out4));
  ROM #(.dataWidth(16)) rom_7 (.addr(controlled_buffer_1_out), .data(rom_2_data), .sel(decoder_1_out5));
  ROM #(.dataWidth(16)) rom_8 (.addr(controlled_buffer_1_out), .data(rom_2_data), .sel(decoder_1_out6));
  ROM #(.dataWidth(16)) rom_9 (.addr(controlled_buffer_1_out), .data(rom_2_data), .sel(decoder_1_out7));
  assign ram_1_data = rom_1_data[9] ? {controlled_buffer_5_out_2, controlled_buffer_5_out} : 16'bz;  // Controlled_Buffer controlled_buffer_3
  RAM #(.dataWidth(16)) ram_5 (
    .addr(register_1_q), .data(ram_1_data), .sel(decoder_2_out4), .clk(clock_1_out), .ld(rom_1_data[9]),
    .clr(HRD_RST));
  RAM #(.dataWidth(16)) ram_6 (
    .addr(register_1_q), .data(ram_1_data), .sel(decoder_2_out5), .clk(clock_1_out), .ld(rom_1_data[9]),
    .clr(HRD_RST));
  RAM #(.dataWidth(16)) ram_7 (
    .addr(register_1_q), .data(ram_1_data), .sel(decoder_2_out6), .clk(clock_1_out), .ld(rom_1_data[9]),
    .clr(HRD_RST));
  RAM #(.dataWidth(16)) ram_8 (
    .addr(register_1_q), .data(ram_1_data), .sel(decoder_2_out7), .clk(clock_1_out), .ld(rom_1_data[9]),
    .clr(HRD_RST));
  Hex_Digit_Display hex_digit_display_1 (.value(controlled_buffer_7_out_4), .dp(1'b0));
  Register register_2 (
    .D(controlled_buffer_5_out_2), .en(rom_1_data[23]), .Q(register_2_q), .clk(clock_1_out), .clr(HRD_RST));
  assign controlled_buffer_4_out = rom_1_data[14] ? rom_1_data[23] : 1'bz;  // Controlled_Buffer controlled_buffer_4
  Pull_Resistor pull_resistor_1 (.node(controlled_buffer_4_out));
  Register IR_MEMH (
    .D(controlled_buffer_5_out_2), .en(rom_1_data[12]), .Q(IR_MEMH_q), .clk(clock_1_out), .clr(HRD_RST));
  Register register_3 (
    .D(controlled_buffer_5_out_2), .en(rom_1_data[11]), .Q(register_3_q), .clk(clock_1_out),
    .clr(rom_1_data[22]));
  assign {controlled_buffer_5_out_2, controlled_buffer_5_out} = rom_1_data[3] ? rom_2_data : 16'bz;  // Controlled_Buffer controlled_buffer_5
  Decoder #(.select(3)) decoder_3 (
    .out0(decoder_3_out0), .out1(decoder_3_out1), .out2(decoder_3_out2), .out3(decoder_3_out3),
    .out4(decoder_3_out4), .out5(decoder_3_out5), .out6(decoder_3_out6), .out7(decoder_3_out7),
    .sel(controlled_buffer_2_out), .en(rom_1_data[18]));
  Decoder #(.select(3)) decoder_4 (
    .out0(decoder_4_out0), .out1(decoder_4_out1), .out2(decoder_4_out2), .out3(decoder_4_out3),
    .out4(decoder_4_out4), .out5(decoder_4_out5), .out6(decoder_4_out6), .out7(decoder_4_out7),
    .sel(register_3_q[5:3]), .en(rom_1_data[21]));
  assign {controlled_buffer_5_out_2, controlled_buffer_5_out} = rom_1_data[8] ? ram_1_data : 16'bz;  // Controlled_Buffer controlled_buffer_6
  Hex_Digit_Display hex_digit_display_2 (.value(controlled_buffer_7_out_2), .dp(1'b0));
  Hex_Digit_Display hex_digit_display_3 (.value(controlled_buffer_7_out_3), .dp(1'b0));
  Register register_4 (
    .D(controlled_buffer_5_out), .en(controlled_buffer_4_out), .Q(register_4_q), .clk(clock_1_out),
    .clr(HRD_RST));
  Register register_5 (
    .D(controlled_buffer_5_out), .en(rom_1_data[10]), .Q(register_5_q), .clk(clock_1_out),
    .clr(rom_1_data[22]));
  Pull_Resistor pull_resistor_2 (.node(decoder_3_out6));
  Pull_Resistor pull_resistor_3 (.node(decoder_3_out5));
  Pull_Resistor pull_resistor_4 (.node(decoder_3_out7));
  Pull_Resistor pull_resistor_5 (.node(decoder_3_out1));
  Pull_Resistor pull_resistor_6 (.node(decoder_3_out2));
  Pull_Resistor pull_resistor_7 (.node(decoder_3_out3));
  Pull_Resistor pull_resistor_8 (.node(decoder_3_out4));
  Pull_Resistor pull_resistor_9 (.node(decoder_4_out4));
  Pull_Resistor pull_resistor_10 (.node(decoder_4_out2));
  Pull_Resistor pull_resistor_11 (.node(decoder_4_out5));
  Pull_Resistor pull_resistor_12 (.node(decoder_4_out3));
  Pull_Resistor pull_resistor_13 (.node(decoder_4_out7));
  Pull_Resistor pull_resistor_14 (.node(decoder_4_out6));
  Hex_Digit_Display hex_digit_display_4 (.value(controlled_buffer_7_out), .dp(1'b0));
  assign {controlled_buffer_7_out_4, controlled_buffer_7_out_3, controlled_buffer_7_out_2, controlled_buffer_7_out} = rom_1_data[13] ? {register_2_q, register_4_q} : 16'bz;  // Controlled_Buffer controlled_buffer_7
  Register IR_MEML (.D(controlled_buffer_5_out), .en(rom_1_data[12]), .Q(IR_MEML_q), .clk(clock_1_out), .clr(HRD_RST));
  assign {controlled_buffer_5_out_2, controlled_buffer_5_out} = OE ? {register_3_q, register_5_q} : 16'bz;  // Controlled_Buffer controlled_buffer_8
  Pull_Resistor pull_resistor_15 (.node(decoder_3_out0));
  Pull_Resistor pull_resistor_16 (.node(decoder_4_out1));
  Pull_Resistor pull_resistor_17 (.node(decoder_4_out0));
  Register register_6 (
    .D(controlled_buffer_5_out_2), .en(controlled_buffer_9_out), .Q(register_6_q), .clk(clock_1_out),
    .clr(HRD_RST));
  assign controlled_buffer_9_out = rom_1_data[14] ? decoder_3_out0 : 1'bz;  // Controlled_Buffer controlled_buffer_9
  Register register_7 (
    .D(controlled_buffer_5_out_2), .en(controlled_buffer_10_out), .Q(register_7_q), .clk(clock_1_out),
    .clr(HRD_RST));
  assign controlled_buffer_10_out = rom_1_data[14] ? decoder_3_out1 : 1'bz;  // Controlled_Buffer controlled_buffer_10
  Register register_8 (
    .D(controlled_buffer_5_out_2), .en(pull_resistor_18_node), .Q(register_8_q), .clk(clock_1_out),
    .clr(HRD_RST));
  Pull_Resistor pull_resistor_18 (.node(pull_resistor_18_node));
  assign pull_resistor_18_node = rom_1_data[14] ? decoder_3_out2 : 1'bz;  // Controlled_Buffer controlled_buffer_11
  Register register_9 (
    .D(controlled_buffer_5_out_2), .en(controlled_buffer_12_out), .Q(register_9_q), .clk(clock_1_out),
    .clr(HRD_RST));
  assign controlled_buffer_12_out = rom_1_data[14] ? decoder_3_out3 : 1'bz;  // Controlled_Buffer controlled_buffer_12
  Register register_10 (
    .D(controlled_buffer_5_out_2), .en(controlled_buffer_13_out), .Q(register_10_q), .clk(clock_1_out),
    .clr(HRD_RST));
  assign controlled_buffer_13_out = rom_1_data[14] ? decoder_3_out4 : 1'bz;  // Controlled_Buffer controlled_buffer_13
  Register register_11 (
    .D(controlled_buffer_5_out_2), .en(controlled_buffer_14_out), .Q(register_11_q), .clk(clock_1_out),
    .clr(HRD_RST));
  assign controlled_buffer_14_out = rom_1_data[14] ? decoder_3_out5 : 1'bz;  // Controlled_Buffer controlled_buffer_14
  Register register_12 (
    .D(controlled_buffer_5_out_2), .en(controlled_buffer_15_out), .Q(register_12_q), .clk(clock_1_out),
    .clr(HRD_RST));
  assign controlled_buffer_15_out = rom_1_data[14] ? decoder_3_out6 : 1'bz;  // Controlled_Buffer controlled_buffer_15
  Register register_13 (
    .D(controlled_buffer_5_out_2), .en(controlled_buffer_16_out), .Q(register_13_q), .clk(clock_1_out),
    .clr(HRD_RST));
  assign controlled_buffer_16_out = rom_1_data[14] ? decoder_3_out7 : 1'bz;  // Controlled_Buffer controlled_buffer_16
  Register register_14 (
    .D(controlled_buffer_5_out), .en(decoder_3_out0), .Q(register_14_q), .clk(clock_1_out), .clr(HRD_RST));
  Pull_Resistor pull_resistor_19 (.node(controlled_buffer_9_out));
  Register register_15 (
    .D(controlled_buffer_5_out), .en(decoder_3_out1), .Q(register_15_q), .clk(clock_1_out), .clr(HRD_RST));
  Pull_Resistor pull_resistor_20 (.node(controlled_buffer_10_out));
  Register register_16 (
    .D(controlled_buffer_5_out), .en(decoder_3_out2), .Q(register_16_q), .clk(clock_1_out), .clr(HRD_RST));
  Register register_17 (
    .D(controlled_buffer_5_out), .en(decoder_3_out3), .Q(register_17_q), .clk(clock_1_out), .clr(HRD_RST));
  Pull_Resistor pull_resistor_21 (.node(controlled_buffer_12_out));
  Register register_18 (
    .D(controlled_buffer_5_out), .en(decoder_3_out4), .Q(register_18_q), .clk(clock_1_out), .clr(HRD_RST));
  Pull_Resistor pull_resistor_22 (.node(controlled_buffer_13_out));
  Register register_19 (
    .D(controlled_buffer_5_out), .en(decoder_3_out5), .Q(register_19_q), .clk(clock_1_out), .clr(HRD_RST));
  Pull_Resistor pull_resistor_23 (.node(controlled_buffer_14_out));
  Register register_20 (
    .D(controlled_buffer_5_out), .en(decoder_3_out6), .Q(register_20_q), .clk(clock_1_out), .clr(HRD_RST));
  Pull_Resistor pull_resistor_24 (.node(controlled_buffer_15_out));
  Register register_21 (
    .D(controlled_buffer_5_out), .en(decoder_3_out7), .Q(register_21_q), .clk(clock_1_out), .clr(HRD_RST));
  Pull_Resistor pull_resistor_25 (.node(controlled_buffer_16_out));
  assign {controlled_buffer_5_out_2, controlled_buffer_5_out} = decoder_4_out0 ? {register_6_q, register_14_q} : 16'bz;  // Controlled_Buffer controlled_buffer_17
  assign {controlled_buffer_5_out_2, controlled_buffer_5_out} = rom_1_data[4] ? register_30_q : 16'bz;  // Controlled_Buffer controlled_buffer_18
  assign {controlled_buffer_5_out_2, controlled_buffer_5_out} = decoder_4_out1 ? {register_7_q, register_15_q} : 16'bz;  // Controlled_Buffer controlled_buffer_19
  Pull_Resistor pull_resistor_26 (.node(rom_1_data[4]));
  assign {controlled_buffer_5_out_2, controlled_buffer_5_out} = decoder_4_out2 ? {register_8_q, register_16_q} : 16'bz;  // Controlled_Buffer controlled_buffer_20
  assign {controlled_buffer_5_out_2, controlled_buffer_5_out} = decoder_4_out3 ? {register_9_q, register_17_q} : 16'bz;  // Controlled_Buffer controlled_buffer_21
  assign {controlled_buffer_5_out_2, controlled_buffer_5_out} = decoder_4_out4 ? {register_10_q, register_18_q} : 16'bz;  // Controlled_Buffer controlled_buffer_22
  assign {controlled_buffer_5_out_2, controlled_buffer_5_out} = decoder_4_out5 ? {register_11_q, register_19_q} : 16'bz;  // Controlled_Buffer controlled_buffer_23
  assign {controlled_buffer_5_out_2, controlled_buffer_5_out} = decoder_4_out6 ? {register_12_q, register_20_q} : 16'bz;  // Controlled_Buffer controlled_buffer_24
  assign {controlled_buffer_5_out_2, controlled_buffer_5_out} = decoder_4_out7 ? {register_13_q, register_21_q} : 16'bz;  // Controlled_Buffer controlled_buffer_25
  Pull_Resistor pull_resistor_27 (.node({controlled_buffer_5_out_2, controlled_buffer_5_out}));
  Decoder #(.select(2)) decoder_5 (
    .out0(decoder_5_out0), .out1(decoder_5_out1), .out2(decoder_5_out2), .out3(decoder_5_out3),
    .sel(rom_1_data_2), .en(rom_1_data[19]));
  not not_2 (not_2_out, rom_1_data[20]);
  Decoder #(.select(2)) decoder_6 (
    .out0(decoder_6_out0), .out1(decoder_6_out1), .out2(decoder_6_out2), .out3(decoder_6_out3),
    .sel(counter_4_q), .en(in_2));
  Counter #(.width(2), .max('h3)) counter_4 (.count(1'b1), .Q(counter_4_q));  // open: load, D, carry, clk, clr
  not not_3 (not_3_out, in_3);
  Comparator #(.width(16)) comparator_1 (
    .a({register_6_q, register_14_q}), .b({controlled_buffer_5_out_2, controlled_buffer_5_out}),
    .gt(adder_1_cout[4]), .eq(adder_1_cout[3]), .lt(adder_1_cout[2]));
  Adder #(.width(16)) adder_1 (
    .a({register_6_q, register_14_q}), .b({controlled_buffer_5_out_2, controlled_buffer_5_out}),
    .out(adder_1_out), .cin(controlled_buffer_34_out), .cout(adder_1_cout[0]));
  Subtractor #(.width(16)) subtractor_1 (
    .a({register_6_q, register_14_q}), .b({controlled_buffer_5_out_2, controlled_buffer_5_out}),
    .out(subtractor_1_out), .bin(controlled_buffer_35_out), .bout(adder_1_cout[1]));
  Multiplier #(.width(16)) multiplier_1 (
    .a({register_6_q, register_14_q}), .b({controlled_buffer_5_out_2, controlled_buffer_5_out}),
    .out(multiplier_1_out));  // open: cin, cout
  Divider #(.width(16)) divider_1 (
    .a({register_6_q, register_14_q}), .b({controlled_buffer_5_out_2, controlled_buffer_5_out}),
    .out(divider_1_out));  // open: upper, rem
  Pull_Resistor pull_resistor_28 (.node(adder_1_cout[2]));
  Pull_Resistor pull_resistor_29 (.node(adder_1_cout[3]));
  Pull_Resistor pull_resistor_30 (.node(adder_1_cout[1]));
  Pull_Resistor pull_resistor_31 (.node(adder_1_cout[0]));
  Pull_Resistor pull_resistor_32 (.node(pull_resistor_32_node));
  Demultiplexer demultiplexer_1 (
    .out0(pull_resistor_32_node), .out1(demultiplexer_1_out1), .in(decoder_5_out0), .sel(not_2_out),
    .en(decoder_5_out0));
  Pull_Resistor pull_resistor_33 (.node(pull_resistor_33_node));
  Demultiplexer demultiplexer_2 (
    .out0(pull_resistor_33_node), .out1(demultiplexer_2_out1), .in(decoder_5_out1), .sel(not_2_out),
    .en(decoder_5_out1));
  Demultiplexer demultiplexer_3 (
    .out0(demultiplexer_3_out0), .out1(demultiplexer_3_out1), .in(decoder_5_out2), .sel(not_2_out),
    .en(decoder_5_out2));
  Demultiplexer demultiplexer_4 (
    .out0(demultiplexer_4_out0), .out1(demultiplexer_4_out1), .in(decoder_5_out3), .sel(not_2_out),
    .en(decoder_5_out3));
  Pull_Resistor pull_resistor_34 (.node(demultiplexer_4_out1));
  Pull_Resistor pull_resistor_35 (.node(pull_resistor_35_node));
  Demultiplexer demultiplexer_5 (
    .out0(pull_resistor_35_node), .out1(demultiplexer_5_out1), .in(decoder_6_out0), .sel(not_3_out),
    .en(decoder_6_out0));
  Pull_Resistor pull_resistor_36 (.node(pull_resistor_36_node));
  Demultiplexer demultiplexer_6 (
    .out0(pull_resistor_36_node), .out1(demultiplexer_6_out1), .in(decoder_6_out1), .sel(not_3_out),
    .en(decoder_6_out1));
  Demultiplexer demultiplexer_7 (
    .out0(demultiplexer_7_out0), .out1(demultiplexer_7_out1), .in(decoder_6_out2), .sel(not_3_out),
    .en(decoder_6_out2));
  Demultiplexer demultiplexer_8 (
    .out0(demultiplexer_8_out0), .out1(demultiplexer_8_out1), .in(decoder_6_out3), .sel(not_3_out),
    .en(decoder_6_out3));
  Pull_Resistor pull_resistor_37 (.node(demultiplexer_8_out1));
  Multiplexer #(.select(2), .width(16)) multiplexer_2 (
    .in0(adder_1_out), .in1(subtractor_1_out), .in2(multiplier_1_out), .in3(divider_1_out),
    .out(multiplexer_2_out), .sel(ARHT), .en(rom_1_data[15]));
  Pull_Resistor pull_resistor_38 (.node(adder_1_cout[6]));
  Pull_Resistor pull_resistor_39 (.node(adder_1_cout[5]));
  Pull_Resistor pull_resistor_40 (.node(adder_1_cout[4]));
  Pull_Resistor pull_resistor_41 (.node(adder_1_cout[7]));
  Register register_22 (
    .D(controlled_buffer_5_out_2), .en(pull_resistor_32_node), .Q(register_22_q), .clk(clock_1_out),
    .clr(HRD_RST));
  Register register_23 (
    .D(controlled_buffer_5_out_2), .en(pull_resistor_33_node), .Q(register_23_q), .clk(clock_1_out),
    .clr(HRD_RST));
  Register register_24 (
    .D(controlled_buffer_5_out_2), .en(demultiplexer_3_out0), .Q(register_24_q), .clk(clock_1_out),
    .clr(HRD_RST));
  Register register_25 (
    .D(controlled_buffer_5_out), .en(demultiplexer_4_out0), .Q(register_25_q), .clk(clock_1_out),
    .clr(HRD_RST));
  Pull_Resistor pull_resistor_42 (.node(demultiplexer_3_out0));
  Register register_26 (
    .D(undriven[15:8]), .en(pull_resistor_35_node), .Q(register_26_q), .clk(clock_1_out), .clr(HRD_RST));
  Register register_27 (
    .D(undriven[15:8]), .en(pull_resistor_36_node), .Q(register_27_q), .clk(clock_1_out), .clr(HRD_RST));
  Register register_28 (
    .D(undriven[15:8]), .en(demultiplexer_7_out0), .Q(register_28_q), .clk(clock_1_out), .clr(HRD_RST));
  Pull_Resistor pull_resistor_43 (.node(demultiplexer_7_out0));
  Register register_29 (
    .D(undriven[15:8]), .en(demultiplexer_8_out0), .Q(register_29_q), .clk(clock_1_out), .clr(HRD_RST));
  Register #(.width(16)) register_30 (
    .D(multiplexer_2_out), .en(rom_1_data[15]), .Q(register_30_q), .clk(clock_1_out), .clr(undriven_2));
  Register register_31 (.D(adder_1_cout), .en(rom_1_data[17]), .Q(register_31_q), .clk(clock_1_out), .clr(undriven_2));
  assign controlled_buffer_5_out_2 = demultiplexer_1_out1 ? register_22_q : 8'bz;  // Controlled_Buffer controlled_buffer_26
  assign controlled_buffer_5_out_2 = demultiplexer_2_out1 ? register_23_q : 8'bz;  // Controlled_Buffer controlled_buffer_27
  assign controlled_buffer_5_out_2 = demultiplexer_3_out1 ? register_24_q : 8'bz;  // Controlled_Buffer controlled_buffer_28
  assign controlled_buffer_5_out_2 = demultiplexer_4_out1 ? register_25_q : 8'bz;  // Controlled_Buffer controlled_buffer_29
  assign controlled_buffer_30_out = demultiplexer_5_out1 ? register_26_q : 8'bz;  // Controlled_Buffer controlled_buffer_30
  assign controlled_buffer_30_out = demultiplexer_6_out1 ? register_27_q : 8'bz;  // Controlled_Buffer controlled_buffer_31
  assign controlled_buffer_30_out = demultiplexer_7_out1 ? register_28_q : 8'bz;  // Controlled_Buffer controlled_buffer_32
  assign controlled_buffer_30_out = demultiplexer_8_out1 ? register_29_q : 8'bz;  // Controlled_Buffer controlled_buffer_33
  assign controlled_buffer_34_out = rom_1_data[16] ? register_31_q[0] : 1'bz;  // Controlled_Buffer controlled_buffer_34
  assign controlled_buffer_35_out = rom_1_data[16] ? register_31_q[1] : 1'bz;  // Controlled_Buffer controlled_buffer_35
  assign controlled_buffer_5_out = demultiplexer_1_out1 ? register_32_q : 8'bz;  // Controlled_Buffer controlled_buffer_36
  Register register_32 (
    .D(controlled_buffer_5_out), .en(pull_resistor_32_node), .Q(register_32_q), .clk(clock_1_out),
    .clr(HRD_RST));
  Pull_Resistor pull_resistor_44 (.node(demultiplexer_1_out1));
  assign controlled_buffer_5_out = demultiplexer_2_out1 ? register_33_q : 8'bz;  // Controlled_Buffer controlled_buffer_37
  Register register_33 (
    .D(controlled_buffer_5_out), .en(pull_resistor_33_node), .Q(register_33_q), .clk(clock_1_out),
    .clr(HRD_RST));
  Pull_Resistor pull_resistor_45 (.node(demultiplexer_2_out1));
  assign controlled_buffer_5_out = demultiplexer_3_out1 ? register_34_q : 8'bz;  // Controlled_Buffer controlled_buffer_38
  Register register_34 (
    .D(controlled_buffer_5_out), .en(demultiplexer_3_out0), .Q(register_34_q), .clk(clock_1_out),
    .clr(HRD_RST));
  Pull_Resistor pull_resistor_46 (.node(demultiplexer_3_out1));
  Register register_35 (
    .D(controlled_buffer_5_out_2), .en(demultiplexer_4_out0), .Q(register_35_q), .clk(clock_1_out),
    .clr(HRD_RST));
  assign controlled_buffer_5_out = demultiplexer_4_out1 ? register_35_q : 8'bz;  // Controlled_Buffer controlled_buffer_39
  Register register_36 (
    .D(undriven[7:0]), .en(pull_resistor_35_node), .Q(register_36_q), .clk(clock_1_out), .clr(HRD_RST));
  assign controlled_buffer_40_out = demultiplexer_5_out1 ? register_36_q : 8'bz;  // Controlled_Buffer controlled_buffer_40
  Pull_Resistor pull_resistor_47 (.node(demultiplexer_5_out1));
  assign controlled_buffer_40_out = demultiplexer_6_out1 ? register_37_q : 8'bz;  // Controlled_Buffer controlled_buffer_41
  Register register_37 (
    .D(undriven[7:0]), .en(pull_resistor_36_node), .Q(register_37_q), .clk(clock_1_out), .clr(HRD_RST));
  Pull_Resistor pull_resistor_48 (.node(demultiplexer_6_out1));
  Register register_38 (
    .D(undriven[7:0]), .en(demultiplexer_7_out0), .Q(register_38_q), .clk(clock_1_out), .clr(HRD_RST));
  assign controlled_buffer_40_out = demultiplexer_7_out1 ? register_38_q : 8'bz;  // Controlled_Buffer controlled_buffer_42
  Pull_Resistor pull_resistor_49 (.node(demultiplexer_7_out1));
  assign controlled_buffer_40_out = demultiplexer_8_out1 ? register_39_q : 8'bz;  // Controlled_Buffer controlled_buffer_43
  Register register_39 (
    .D(undriven[7:0]), .en(demultiplexer_8_out0), .Q(register_39_q), .clk(clock_1_out), .clr(HRD_RST));

  // Notes on the sheet:
  //   0 0001:    LDI [b]
  //   0 0002:    LDI [W]
  //   contents of rom_1 (hex, n*v repeats v):
  //   3 40c 400000 13*0 c0180008 c00c0000 0 400000 12*0 3 4400c 0 400000
  //   B1
  //   contents of rom_2 (hex, n*v repeats v):
  //   0 2 abcd 0 0 22 3549 42 0 0 42 ffff
  //   B2
  //   B3
  //   B4
  //   B1
  //   B2
  //   B3
  //   B4
  //   B5
  //   B6
  //   B7
  //   B8
  //   B5
  //   B6
  //   B7
  //   B8
  //   OH
  //   IRH
  //   OL
  //   IRL
  //   AH
  //   BH
  //   CH
  //   DH
  //   R1H
  //   R2H
  //   R3H
  //   R4H
  //   AL
  //   BL
  //   CL
  //   DL
  //   R1L
  //   R2L
  //   R3L
  //   R4L
  //   SP0
  //   SP1
  //   SP2
  //   SP3
endmodule
